// Logisim project archiMinimale.circ as structural Verilog: 1 circuit, main circuit main
module main (
  input  H,
  input  Raz
);

  wire and_4_out, and_5_out, beq, bgtz, blez, bne, branch, emem, ereg, immrt, multiplexer_5_out, not_1_out,
       not_2_out, not_3_out, or_1_out, registerfile_1_p8, rtrd, tunnel, ualmem;
  wire [3:0] op;
  wire [4:0] multiplexer_1_out, num_rd, num_rs, num_rt, shamt;
  wire [5:0] co, nf;
  wire [31:0] adder_1_p1, adder_1_p2, adder_1_p3, imm32, mips_ram_1_p7, multiplexer_3_out, multiplexer_4_out,
       pc, res, rs, rt, w;

  not not_1 (not_1_out, ereg);
  // PLA pla_1: pin names not known; wires that end beside it: co, {emem, ereg, branch, ualmem, immrt, rtrd}
  Multiplexer #(.width(5), .enable("false")) multiplexer_1 (
    .in0(num_rt), .in1(num_rd), .out(multiplexer_1_out), .sel(rtrd));
  // RegisterFile registerfile_1: pin names not known; wires that end beside it: w, H, not_1_out, multiplexer_1_out, num_rs, num_rt, Raz, registerfile_1_p8, rt
  // MIPS_RAM mips_ram_1: pin names not known; wires that end beside it: res[19:0], rt, emem, 1'b1, H, Raz, mips_ram_1_p7
  Multiplexer #(.width(32), .enable("false")) multiplexer_2 (.in0(res), .in1(mips_ram_1_p7), .out(w), .sel(ualmem));
  // PLA PLA_2: pin names not known; wires that end beside it: {nf, co}, op
  Multiplexer #(.width(32), .enable("false")) multiplexer_3 (
    .in0(imm32), .in1(rt), .out(multiplexer_3_out), .sel(immrt));
  // MIPS_ALU mips_alu_1: pin names not known; wires that end beside it: registerfile_1_p8, multiplexer_3_out, op, tunnel, res
  // PLA PLA_3: pin names not known
  // MIPSProgramROM mipsprogramrom_1: pin names not known; wires that end beside it: pc, {co, num_rs, num_rt, num_rd, shamt, nf}
  // Probe on {co, num_rs, num_rt, num_rd, shamt, nf}
  // Probe on rtrd
  // Probe on immrt
  // Probe on ualmem
  // Probe on branch
  not not_2 (not_2_out, ereg);
  // Probe on not_2_out
  // Probe on emem
  // Probe on op
  // Probe on res
  assign imm32 = {{16{num_rd[4]}}, {num_rd, shamt, nf}};  // Bit_Extender bit_extender_1
  // Probe on pc
  // Probe on co
  // Probe on num_rs
  // Probe on rs
  // Probe on num_rt
  // Probe on rt
  // Probe on num_rd
  // Probe on shamt
  // Probe on nf
  // Probe on imm32
  and and_1 (beq, tunnel, branch);
  Multiplexer #(.width(32), .enable("false")) multiplexer_4 (
    .in0(adder_1_p1), .in1(adder_1_p3), .out(multiplexer_4_out), .sel(and_5_out));
  // Adder adder_1: pin names not known; wires that end beside it: adder_1_p1, adder_1_p2, adder_1_p3
  and and_2 (bne, ~tunnel, branch);  // AND_Gate
  // Adder adder_2: pin names not known; wires that end beside it: 32'h4, pc, adder_1_p1
  Register #(.width(32), .trigger("falling")) register_1 (.D(multiplexer_4_out), .en(1'b1), .Q(pc), .clk(H), .clr(Raz));
  Shifter #(.width(32)) shifter_1 (.in(imm32), .\dist (5'b00010), .out(adder_1_p2));
  and and_3 (blez, or_1_out, branch);
  or or_1 (or_1_out, tunnel, and_4_out);
  and and_4 (and_4_out, rtrd, rs[31]);
  and and_5 (and_5_out, branch, not_3_out);
  not not_3 (not_3_out, tunnel);
  and and_6 (bgtz, ~or_1_out, branch);  // AND_Gate
  Multiplexer #(.select(2), .enable("false")) multiplexer_5 (
    .in0(beq), .in1(bne), .in2(blez), .in3(bgtz), .out(multiplexer_5_out), .sel(co[1:0]));

  // Other names for the same wires on the sheet: _0 = Raz

  // Notes on the sheet:
  //   mémoire de donnée
  //   Meh
  //   commandes
  //   vérifications
  //   décomposition de l'opération MIPS
  //   on suppose que l'on a la valeur de rs UNIQUEMENT si on utilise rd --> ???
  //   détermination de la prochaine instruction (pc)
endmodule
